# Fritzing sketch V_1.0_(SEN_READINGS) (saved by Fritzing 0.9.3b)
breadboards: 1

parts:
  U1 = ESP32S-HiLetgo [part_number=ESP32S-HiLetgo]
  OLED_I2C1 = OLED 128x64 I2C Monochrome Display
  Mod1 = gy-906
  M1 = MAX30102

nets:
  VDD: U1.3.3, U1.EN, OLED_I2C1.VDD, Mod1.VIN
  GND: U1.GND, U1.GPIO21, U1.GPIO23, OLED_I2C1.GND, Mod1.GND, M1.VIN, M1.GND
  N1: U1.GPIO1, U1.GPIO22

custom parts:
  ESP32S-HiLetgo: HiLetgo ESP-WROOM-32 ESP32 ESP-32S Development Board 2.4GHz Dual-Mode WiFi + Bluetooth Dual Cores Microcontroller The ESP32 integrated with Antenna switches, RF Balun, power amplifiers, low-noise amplifiers, filters, and management modules, and the entire solution occupies the least area of PCB. 2.4 GHz Wi-Fi plus Bluetooth dual-mode chip, with TSMC Ultra-low power consumption 40nm technology,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
  gy-906: gy-906 Non-contact PIR I2C interface temperature sensor breakout board.
  MAX30102: Oximeter module using the MAX30102 chip. You may wish to read (and check your module) this post on power problems with these modules: https://reedpaper.wordpress.com/2018/08/22/pulse-oximeter-max30100-max30102-how-to-fix-wrong-board/ . As usual, if you want the mounting holes in pcb, you need to drag a hole over the pad in silkscreen to actually drill the hole (by default they are not drilled)
