# Fritzing sketch v_10.0 (saved by Fritzing 0.9.3b)
breadboards: 1

parts:
  U1 = ESP32S-HiLetgo [part_number=ESP32S-HiLetgo]
  OLED_I2C1 = OLED 128x64 I2C Monochrome Display
  Mod1 = gy-906
  M1 = MAX30102
  LED1 = LED - 5mm [color="Orange (620nm)" package="5 mm [THT]"]  # not connected
  LED2 = LED - 5mm [color="Green (555nm)" package="5 mm [THT]"]
  R2 = Resistor [tolerance=±5% resistance=220 package=THT]
  SIM800L1 = SIM800L
  Part1 = MicroSD Card Module
  MIC1 = Microphone
  SPKR1 = Loudspeaker
  S1 = Pushbutton [package="[SMD]"]
  S2 = Pushbutton [package="[SMD]"]
  R3 = Resistor [tolerance=±5% resistance=220 package=THT]
  R4 = Resistor [tolerance=±5% resistance=220 package=THT]
  S3 = Pushbutton [package="[SMD]"]
  R5 = Resistor [tolerance=±5% resistance=220 package=THT]
  U2 = LIPO-2000mAh [package=lipo-2000]
  R1 = Resistor [tolerance=±5% resistance=220 package=THT]

nets:
  VIN: U1.3.3, U1.EN, OLED_I2C1.VDD, Mod1.VIN, M1.VIN, SIM800L1.VCC, Part1.VCC, S1.Pin_1, S1.Pin_2, S2.Pin_1, S2.Pin_2, S3.Pin_1, S3.Pin_2, U2.+
  N1: U1.GPIO33, R1.Pin_0
  N2: U1.GPIO25, R2.Pin_0
  N3: U1.GPIO27, S1.Pin_3, S1.Pin_4, R3.Pin_1
  N4: U1.GPIO14, S2.Pin_3, S2.Pin_4, R4.Pin_0
  N5: U1.GPIO12, S3.Pin_3, S3.Pin_4, R5.Pin_0
  GND: U1.GND, U1.GPIO21, U1.GPIO23, OLED_I2C1.GND, Mod1.GND, M1.GND, LED2.cathode, SIM800L1.GND, Part1.GND, Part1.MOSI, R3.Pin_0, R4.Pin_1, R5.Pin_1, U2.-
  N6: U1.GPIO16, SIM800L1.TXD
  N7: U1.GPIO17, SIM800L1.RXD
  N8: U1.GPIO5, Part1.CS
  N9: U1.GPIO18, Part1.SCK
  N10: U1.GPIO19, Part1.MISO
  N11: SIM800L1.MCP, MIC1.pin2
  N12: SIM800L1.MCN, MIC1.pin1
  N13: SIM800L1.SPKP, SPKR1.pin1
  N14: SIM800L1.SPKN, SPKR1.pin2

custom parts:
  ESP32S-HiLetgo: HiLetgo ESP-WROOM-32 ESP32 ESP-32S Development Board 2.4GHz Dual-Mode WiFi + Bluetooth Dual Cores Microcontroller The ESP32 integrated with Antenna switches, RF Balun, power amplifiers, low-noise amplifiers, filters, and management modules, and the entire solution occupies the least area of PCB. 2.4 GHz Wi-Fi plus Bluetooth dual-mode chip, with TSMC Ultra-low power consumption 40nm technology,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
  gy-906: gy-906 Non-contact PIR I2C interface temperature sensor breakout board.
  MAX30102: Oximeter module using the MAX30102 chip. You may wish to read (and check your module) this post on power problems with these modules: https://reedpaper.wordpress.com/2018/08/22/pulse-oximeter-max30100-max30102-how-to-fix-wrong-board/ . As usual, if you want the mounting holes in pcb, you need to drag a hole over the pad in silkscreen to actually drill the hole (by default they are not drilled)
  SIM800L: SIM800L is a miniature cellular module which allows for GPRS transmission, sending and receiving SMS and making and receiving voice calls. Low cost and small footprint and quad band frequency support make this module perfect solution for any project that require long range connectivity. After connecting power module boots up, searches for cellular network and login automatically. On board LED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
