# Fritzing sketch V_4.0_(LED_INDICATOR) (saved by Fritzing 0.9.4)
breadboards: 1

parts:
  U1 = ESP32S-HiLetgo [part_number=ESP32S-HiLetgo]
  OLED_I2C1 = OLED 128x64 I2C Monochrome Display
  Mod1 = gy-906
  M1 = MAX30102
  LED1 = LED - 5mm [color="Orange (620nm)" package="5 mm [THT]"]
  LED2 = LED - 5mm [color="Green (555nm)" package="5 mm [THT]"]
  R1 = Resistor [tolerance=±5% resistance=220 package=THT]
  R2 = Resistor [tolerance=±5% resistance=220 package=THT]  # not connected
  SIM800L1 = SIM800L
  Part1 = MicroSD Card Module
  MIC1 = Microphone
  SPKR1 = Loudspeaker

nets:
  VIN: U1.3.3, U1.EN, OLED_I2C1.VDD, Mod1.VIN, M1.VIN, SIM800L1.VCC, Part1.VCC
  N1: U1.GPIO26, LED1.anode
  N2: U1.GPIO27, LED2.anode
  GND: U1.GND, U1.GPIO21, U1.GPIO23, OLED_I2C1.GND, Mod1.GND, M1.GND, R1.Pin_0, SIM800L1.GND, Part1.GND, Part1.MOSI
  N3: U1.GPIO16, SIM800L1.TXD
  N4: U1.GPIO17, SIM800L1.RXD
  N5: U1.GPIO5, Part1.CS
  N6: U1.GPIO18, Part1.SCK
  N7: U1.GPIO19, Part1.MISO
  N8: U1.GPIO1, U1.GPIO22
  N9: SIM800L1.MCP, MIC1.pin2
  N10: SIM800L1.MCN, MIC1.pin1
  N11: SIM800L1.SPKP, SPKR1.pin1
  N12: SIM800L1.SPKN, SPKR1.pin2

custom parts:
  ESP32S-HiLetgo: HiLetgo ESP-WROOM-32 ESP32 ESP-32S Development Board 2.4GHz Dual-Mode WiFi + Bluetooth Dual Cores Microcontroller The ESP32 integrated with Antenna switches, RF Balun, power amplifiers, low-noise amplifiers, filters, and management modules, and the entire solution occupies the least area of PCB. 2.4 GHz Wi-Fi plus Bluetooth dual-mode chip, with TSMC Ultra-low power consumption 40nm technology,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
  gy-906: gy-906 Non-contact PIR I2C interface temperature sensor breakout board.
  MAX30102: Oximeter module using the MAX30102 chip. You may wish to read (and check your module) this post on power problems with these modules: https://reedpaper.wordpress.com/2018/08/22/pulse-oximeter-max30100-max30102-how-to-fix-wrong-board/ . As usual, if you want the mounting holes in pcb, you need to drag a hole over the pad in silkscreen to actually drill the hole (by default they are not drilled)
  SIM800L: SIM800L is a miniature cellular module which allows for GPRS transmission, sending and receiving SMS and making and receiving voice calls. Low cost and small footprint and quad band frequency support make this module perfect solution for any project that require long range connectivity. After connecting power module boots up, searches for cellular network and login automatically. On board LED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
